// Logisim project 4 bit Universal Shift Register.circ as structural Verilog: 2 circuits, main circuit 4 bit Universal Shift Register
module _4_bit_Universal_Shift_Register (
  input  CLOCK,
  input  CLEAR,
  input  [1:0] S1__S0,
  input  in_4,
  input  in_5,
  input  I4,
  input  I3,
  input  I2,
  input  I1,
  output A4,
  output A3,
  output A2,
  output A1
);

  wire multiplexer_1_out, multiplexer_2_out, multiplexer_3_out, multiplexer_4_out;

  Multiplexer #(.select(2)) multiplexer_1 (
    .in0(A4), .in1(in_4), .in2(A3), .in3(I4), .out(multiplexer_1_out), .sel(S1__S0));  // open: en
  D_Flip_Flop d_ff_1 (.clk(CLOCK), .D(multiplexer_1_out), .Q(A4), .reset(CLEAR));  // open: Qn, preset, en
  Multiplexer #(.select(2)) multiplexer_2 (
    .in0(A3), .in1(A4), .in2(A2), .in3(I3), .out(multiplexer_2_out), .sel(S1__S0));  // open: en
  D_Flip_Flop d_ff_2 (.clk(CLOCK), .D(multiplexer_2_out), .Q(A3), .reset(CLEAR));  // open: Qn, preset, en
  Multiplexer #(.select(2)) multiplexer_3 (
    .in0(A2), .in1(A3), .in2(A1), .in3(I2), .out(multiplexer_3_out), .sel(S1__S0));  // open: en
  D_Flip_Flop d_ff_3 (.clk(CLOCK), .D(multiplexer_3_out), .Q(A2), .reset(CLEAR));  // open: Qn, preset, en
  Multiplexer #(.select(2)) multiplexer_4 (
    .in0(A1), .in1(A2), .in2(in_5), .in3(I1), .out(multiplexer_4_out), .sel(S1__S0));  // open: en
  D_Flip_Flop d_ff_4 (.clk(CLOCK), .D(multiplexer_4_out), .Q(A1), .reset(CLEAR));  // open: Qn, preset, en

  // Notes on the sheet:
  //   Serial  input for Shift Right
  //   F4
  //   F3
  //   Design of a 4 bit Universal Shift Register
  //   F2
  //   F1
  //   Serial input for Shift Left
  //   Md Saiyem Raiyan
  //   ID: 2012468642
endmodule

module main (
  input  in_1,
  input  in_2,
  input  in_3,
  input  in_4,
  input  in_5,
  input  in_6,
  input  [1:0] in_7,
  output out_8,
  output out_9,
  output out_10,
  output out_11
);

  wire button_1_out, clock_1_out;

  Clock clock_1 (.out(clock_1_out));
  _4_bit_Universal_Shift_Register u_4_bit_universal_shift_register_1 (
    .CLOCK(clock_1_out), .CLEAR(in_6), .S1__S0(in_7), .in_4(in_5), .in_5(button_1_out), .A4(out_11),
    .A3(out_10), .A2(out_9), .A1(out_8), .I4(in_1), .I3(in_2), .I2(in_3), .I1(in_4));
  Button button_1 (.out(button_1_out));

  // Notes on the sheet:
  //   Design of a 4 bit Universal Shift Register
  //   Md Saiyem Raiyan
  //   ID: 2012468642
endmodule
