// Logisim project CSE332L.13-2012468642-Md Saiyem Raiyan-LAB 5-Design a 4 bit register and 4 bit ALU.circ as structural Verilog: 3 circuits, main circuit main
module main (
  input  [3:0] in_1,
  input  [3:0] in_2,
  input  [2:0] in_3,
  input  [3:0] in_4,
  input  in_5,
  input  in_6,
  input  [1:0] in_7,
  input  [2:0] in_8,
  input  [2:0] in_9,
  output [3:0] out_10,
  output [3:0] out_11,
  output [3:0] out_12
);

  _4_bit_register u_4_bit_register_1 (
    .Input(in_2), .Write(in_3), .Clock(in_5), .Read_Data_1(out_10), .in_1(in_8), .Read_Data_2(out_11),
    .in_4(in_9), .Write_Data(in_6));
  _4_Bit_ALU u_4_bit_alu_1 (.Input_1(in_4), .Input_2(in_1), .Operation_Select_Bits(in_7), .Output(out_12));

  // Notes on the sheet:
  //   4 Bit Register
  //   4 Bit ALU
endmodule

module _4_bit_register (
  input  [2:0] in_1,
  input  [3:0] Input,
  input  [2:0] Write,
  input  [2:0] in_4,
  input  Write_Data,
  input  Clock,
  output [3:0] Read_Data_1,
  output [3:0] Read_Data_2
);

  wire and_1_out, decoder_1_out0, decoder_1_out1, decoder_1_out2, decoder_1_out3, decoder_1_out4,
       decoder_1_out5, decoder_1_out6, decoder_1_out7;
  wire [3:0] register_1_q, register_2_q, register_3_q, register_4_q, register_5_q, register_6_q,
       register_7_q, register_8_q;

  and and_1 (and_1_out, Write_Data, Clock);
  Decoder #(.select(3)) decoder_1 (
    .out0(decoder_1_out0), .out1(decoder_1_out1), .out2(decoder_1_out2), .out3(decoder_1_out3),
    .out4(decoder_1_out4), .out5(decoder_1_out5), .out6(decoder_1_out6), .out7(decoder_1_out7), .sel(Write));  // open: en
  Register #(.width(4)) register_1 (.D(Input), .en(decoder_1_out0), .Q(register_1_q), .clk(and_1_out));  // open: clr
  Register #(.width(4)) register_2 (.D(Input), .en(decoder_1_out1), .Q(register_2_q), .clk(and_1_out));  // open: clr
  Register #(.width(4)) register_3 (.D(Input), .en(decoder_1_out2), .Q(register_3_q), .clk(and_1_out));  // open: clr
  Register #(.width(4)) register_4 (.D(Input), .en(decoder_1_out3), .Q(register_4_q), .clk(and_1_out));  // open: clr
  Register #(.width(4)) register_5 (.D(Input), .en(decoder_1_out4), .Q(register_5_q), .clk(and_1_out));  // open: clr
  Register #(.width(4)) register_6 (.D(Input), .en(decoder_1_out5), .Q(register_6_q), .clk(and_1_out));  // open: clr
  Register #(.width(4)) register_7 (.D(Input), .en(decoder_1_out6), .Q(register_7_q), .clk(and_1_out));  // open: clr
  Register #(.width(4)) register_8 (.D(Input), .en(decoder_1_out7), .Q(register_8_q), .clk(and_1_out));  // open: clr
  Multiplexer #(.select(3), .width(4)) multiplexer_1 (
    .in0(register_1_q), .in1(register_2_q), .in2(register_3_q), .in3(register_4_q), .in4(register_5_q),
    .in5(register_6_q), .in6(register_7_q), .in7(register_8_q), .out(Read_Data_1), .sel(in_1));  // open: en
  Multiplexer #(.select(3), .width(4)) multiplexer_2 (
    .in0(register_1_q), .in1(register_2_q), .in2(register_3_q), .in3(register_4_q), .in4(register_5_q),
    .in5(register_6_q), .in6(register_7_q), .in7(register_8_q), .out(Read_Data_2), .sel(in_4));  // open: en

  // Notes on the sheet:
  //   Read Register 1
  //   Read Register 2
endmodule

module _4_Bit_ALU (
  input  [3:0] Input_1,
  input  [3:0] Input_2,
  input  [1:0] Operation_Select_Bits,
  output [3:0] Output
);

  wire [3:0] adder_1_out, and_1_out, or_1_out, subtractor_1_out;

  assign and_1_out = Input_1 & Input_2;  // AND_Gate and_1, 4 bits wide
  assign or_1_out = Input_1 | Input_2;  // OR_Gate or_1, 4 bits wide
  Adder #(.width(4)) adder_1 (.a(Input_1), .b(Input_2), .out(adder_1_out));  // open: cin, cout
  Subtractor #(.width(4)) subtractor_1 (.a(Input_1), .b(Input_2), .out(subtractor_1_out));  // open: bin, bout
  Multiplexer #(.select(2), .width(4)) multiplexer_1 (
    .in0(and_1_out), .in1(or_1_out), .in2(adder_1_out), .in3(subtractor_1_out), .out(Output),
    .sel(Operation_Select_Bits));  // open: en

  // Notes on the sheet:
  //   4 Bit ALU
endmodule
