// Logisim project CSE332L.13-2012468642-Md Saiyem Raiyan-LAB1-Design of a 2 bit logic unit .circ as structural Verilog: 2 circuits, main circuit main
// A1
module main (
  input  in_1,
  input  in_2,
  input  [1:0] in_3,
  input  in_4,
  input  in_5,
  output out_6,
  output out_7
);

  circuit circuit_1 (.A1(in_1), .A0(in_2), .S1_S0(in_3), .A0_2(in_4), .B0(in_5), .F1(out_6), .F0(out_7));
endmodule

module circuit (
  input  A1,
  input  A0,
  input  [1:0] S1_S0,
  input  A0_2,
  input  B0,
  output F1,
  output F0
);

  wire and_1_out, and_2_out, not_1_out, not_2_out, or_1_out, or_2_out, xor_1_out, xor_2_out;

  and and_1 (and_1_out, A1, A0);
  or or_1 (or_1_out, A1, A0);
  xor xor_1 (xor_1_out, A1, A0);
  not not_1 (not_1_out, A1);
  and and_2 (and_2_out, A0_2, B0);
  or or_2 (or_2_out, A0_2, B0);
  xor xor_2 (xor_2_out, A0_2, B0);
  not not_2 (not_2_out, A0_2);
  Multiplexer #(.select(2)) multiplexer_1 (
    .in0(and_1_out), .in1(or_1_out), .in2(xor_1_out), .in3(not_1_out), .out(F1), .sel(S1_S0));  // open: en
  Multiplexer #(.select(2)) multiplexer_2 (
    .in0(and_2_out), .in1(or_2_out), .in2(xor_2_out), .in3(not_2_out), .out(F0), .sel(S1_S0));  // open: en
endmodule
