// Logisim project CSE332L.13-2012468642-Md Saiyem Raiyan-LAB2- Design of a 2-bit Arithmetic unit.circ as structural Verilog: 2 circuits, main circuit 2 bit arithmatic logic unit
module _2_bit_arithmatic_logic_unit (
  input  C_in,
  input  [1:0] S1_S0,
  input  B0,
  input  A0,
  input  A1,
  input  B1,
  output D0,
  output D1,
  output C_out
);

  wire adder_1_cout, multiplexer_1_out, multiplexer_2_out, not_1_out, not_2_out;

  not not_1 (not_1_out, B0);
  not not_2 (not_2_out, B1);
  Multiplexer #(.select(2)) multiplexer_1 (
    .in0(B0), .in1(not_1_out), .in2(1'b0), .in3(1'b1), .out(multiplexer_1_out), .sel(S1_S0));  // open: en
  Multiplexer #(.select(2)) multiplexer_2 (
    .in0(B1), .in1(not_2_out), .in2(1'b0), .in3(1'b1), .out(multiplexer_2_out), .sel(S1_S0));  // open: en
  Adder #(.width(1)) adder_1 (.a(A0), .b(multiplexer_1_out), .out(D0), .cin(C_in), .cout(adder_1_cout));
  Adder #(.width(1)) adder_2 (.a(A1), .b(multiplexer_2_out), .out(D1), .cin(adder_1_cout), .cout(C_out));

  // Notes on the sheet:
  //   2 bits Arithmetic logic unit
  //   Md Saiyem Raiyan
  //   ID: 2012468642
endmodule

module main (
  input  [1:0] in_1,
  input  in_2,
  input  in_3,
  input  in_4,
  input  in_5,
  input  in_6,
  output out_7,
  output out_8,
  output out_9
);

  _2_bit_arithmatic_logic_unit u_2_bit_arithmatic_logic_unit_1 (
    .C_in(in_2), .S1_S0(in_1), .B0(in_6), .A0(in_4), .A1(in_3), .B1(in_5), .D0(out_8), .D1(out_7),
    .C_out(out_9));

  // Notes on the sheet:
  //   2 bits Arithmetic Logic Unit
  //   Md Saiyem Raiyan
  //   ID: 2012468642
endmodule
