// Logisim project Single cycle datapath for I-type with main control.circ as structural Verilog: 7 circuits, main circuit main
module main (
  input  [3:0] in_1,
  input  [2:0] in_2,
  input  [3:0] in_3,
  input  [3:0] in_4,
  input  in_5,
  input  in_6,
  input  [1:0] in_7,
  input  [2:0] in_8,
  input  [2:0] in_9,
  output [3:0] out_10,
  output [3:0] out_11,
  output [3:0] out_12
);

  _4_bit_register u_4_bit_register_1 (
    .Write_Register(in_2), .Clock(in_6), .Read_Data_1(out_10), .in_1(in_8), .Read_Data_2(out_11),
    .in_4(in_9), .Write(in_5), .Write_Data(in_3));
  _4_Bit_ALU u_4_bit_alu_1 (.Input_1(in_1), .Input_2(in_4), .Operation_Select_Bits(in_7), .Output(out_12));

  // Notes on the sheet:
  //   4 Bit Register
  //   4 Bit ALU
endmodule

module _4_bit_register (
  input  [2:0] in_1,
  input  [2:0] Write_Register,
  input  [3:0] Write_Data,
  input  [2:0] in_4,
  input  Write,
  input  Clock,
  output [3:0] Read_Data_1,
  output [3:0] Read_Data_2
);

  wire and_1_out, decoder_1_out0, decoder_1_out1, decoder_1_out2, decoder_1_out3, decoder_1_out4,
       decoder_1_out5, decoder_1_out6, decoder_1_out7;
  wire [3:0] register_1_q, register_2_q, register_3_q, register_4_q, register_5_q, register_6_q,
       register_7_q, register_8_q;

  Decoder #(.select(3)) decoder_1 (
    .out0(decoder_1_out0), .out1(decoder_1_out1), .out2(decoder_1_out2), .out3(decoder_1_out3),
    .out4(decoder_1_out4), .out5(decoder_1_out5), .out6(decoder_1_out6), .out7(decoder_1_out7),
    .sel(Write_Register));  // open: en
  and and_1 (and_1_out, Write, Clock);
  Register #(.width(4)) register_1 (
    .D(Write_Data), .en(decoder_1_out0), .Q(register_1_q), .clk(and_1_out));  // open: clr
  Register #(.width(4)) register_2 (
    .D(Write_Data), .en(decoder_1_out1), .Q(register_2_q), .clk(and_1_out));  // open: clr
  Register #(.width(4)) register_3 (
    .D(Write_Data), .en(decoder_1_out2), .Q(register_3_q), .clk(and_1_out));  // open: clr
  Register #(.width(4)) register_4 (
    .D(Write_Data), .en(decoder_1_out3), .Q(register_4_q), .clk(and_1_out));  // open: clr
  Register #(.width(4)) register_5 (
    .D(Write_Data), .en(decoder_1_out4), .Q(register_5_q), .clk(and_1_out));  // open: clr
  Register #(.width(4)) register_6 (
    .D(Write_Data), .en(decoder_1_out5), .Q(register_6_q), .clk(and_1_out));  // open: clr
  Register #(.width(4)) register_7 (
    .D(Write_Data), .en(decoder_1_out6), .Q(register_7_q), .clk(and_1_out));  // open: clr
  Register #(.width(4)) register_8 (
    .D(Write_Data), .en(decoder_1_out7), .Q(register_8_q), .clk(and_1_out));  // open: clr
  Multiplexer #(.select(3), .width(4)) multiplexer_1 (
    .in0(register_1_q), .in1(register_2_q), .in2(register_3_q), .in3(register_4_q), .in4(register_5_q),
    .in5(register_6_q), .in6(register_7_q), .in7(register_8_q), .out(Read_Data_1), .sel(in_1));  // open: en
  Multiplexer #(.select(3), .width(4)) multiplexer_2 (
    .in0(register_1_q), .in1(register_2_q), .in2(register_3_q), .in3(register_4_q), .in4(register_5_q),
    .in5(register_6_q), .in6(register_7_q), .in7(register_8_q), .out(Read_Data_2), .sel(in_4));  // open: en

  // Notes on the sheet:
  //   Read Register 1
  //   Read Register 2
  //   4 Bit Register
endmodule

module _4_Bit_ALU (
  input  [3:0] Input_1,
  input  [3:0] Input_2,
  input  [1:0] Operation_Select_Bits,
  output [3:0] Output
);

  wire [3:0] adder_1_out, and_1_out, or_1_out, subtractor_1_out;

  assign and_1_out = Input_1 & Input_2;  // AND_Gate and_1, 4 bits wide
  assign or_1_out = Input_1 | Input_2;  // OR_Gate or_1, 4 bits wide
  Adder #(.width(4)) adder_1 (.a(Input_1), .b(Input_2), .out(adder_1_out));  // open: cin, cout
  Subtractor #(.width(4)) subtractor_1 (.a(Input_1), .b(Input_2), .out(subtractor_1_out));  // open: bin, bout
  Multiplexer #(.select(2), .width(4)) multiplexer_1 (
    .in0(and_1_out), .in1(or_1_out), .in2(adder_1_out), .in3(subtractor_1_out), .out(Output),
    .sel(Operation_Select_Bits));  // open: en

  // Notes on the sheet:
  //   4 Bit ALU
endmodule

module single_cycle_datapath_for_R_type_instruction (
  input  in_1,
  output [3:0] Output
);

  wire clock_1_out;
  wire [2:0] adder_1_out, register_1_q;
  wire [3:0] n4_bit_register_1_read_data_1, n4_bit_register_1_read_data_2;
  wire [12:0] rom_1_data;

  Adder #(.width(3)) adder_1 (.a(register_1_q), .b(3'b001), .out(adder_1_out));  // open: cin, cout
  Register #(.width(3)) register_1 (.D(adder_1_out), .Q(register_1_q), .clk(clock_1_out));  // open: en, clr
  ROM #(.addrWidth(3), .dataWidth(13)) rom_1 (.addr(register_1_q), .data(rom_1_data));  // open: sel
  Clock clock_1 (.out(clock_1_out));
  _4_bit_register u_4_bit_register_1 (
    .Write_Register(rom_1_data[2:0]), .Clock(clock_1_out), .Read_Data_1(n4_bit_register_1_read_data_1),
    .in_1(rom_1_data[8:6]), .Read_Data_2(n4_bit_register_1_read_data_2), .in_4(rom_1_data[5:3]),
    .Write(in_1), .Write_Data(Output));
  _4_Bit_ALU u_4_bit_alu_1 (
    .Input_1(n4_bit_register_1_read_data_1), .Input_2(n4_bit_register_1_read_data_2),
    .Operation_Select_Bits(rom_1_data[10:9]), .Output(Output));

  // Notes on the sheet:
  //   Program Counter
  //   contents of rom_1 (hex, n*v repeats v):
  //   611 258
  //   Single cycle datapath for R-type instructions
endmodule

module single_cycle_datapath_for_I_type_instruction (
  input  Memory_Write,
  input  Memory_Read,
  input  in_3,
  output [3:0] Output,
  output [3:0] Output_2
);

  wire clock_1_out;
  wire [2:0] adder_1_out, register_1_q;
  wire [3:0] bit_extender_1_out, n4_bit_register_1_read_data_1, n4_bit_register_1_read_data_2;
  wire [12:0] rom_1_data;

  Register #(.width(3)) register_1 (.D(adder_1_out), .Q(register_1_q), .clk(clock_1_out));  // open: en, clr
  Adder #(.width(3)) adder_1 (.a(register_1_q), .b(3'b001), .out(adder_1_out));  // open: cin, cout
  RAM #(.addrWidth(4), .dataWidth(4), .bus("separate")) ram_1 (
    .addr(Output_2), .din(n4_bit_register_1_read_data_2), .data(Output), .str(Memory_Write),
    .clk(clock_1_out), .ld(Memory_Read));  // open: sel, clr
  ROM #(.addrWidth(3), .dataWidth(13)) rom_1 (.addr(register_1_q), .data(rom_1_data));  // open: sel
  Clock clock_1 (.out(clock_1_out));
  assign bit_extender_1_out = {{1{1'b0}}, rom_1_data[2:0]};  // Bit_Extender bit_extender_1
  _4_bit_register u_4_bit_register_1 (
    .Write_Register(rom_1_data[5:3]), .Clock(clock_1_out), .Read_Data_1(n4_bit_register_1_read_data_1),
    .in_1(rom_1_data[8:6]), .Read_Data_2(n4_bit_register_1_read_data_2), .in_4(rom_1_data[5:3]),
    .Write(in_3), .Write_Data(Output));
  _4_Bit_ALU u_4_bit_alu_1 (
    .Input_1(n4_bit_register_1_read_data_1), .Input_2(bit_extender_1_out),
    .Operation_Select_Bits(rom_1_data[10:9]), .Output(Output_2));

  // Notes on the sheet:
  //   Program Counter
  //   contents of rom_1 (hex, n*v repeats v):
  //   c8b c99
  //   Single cycle Datapath for I-type instructions
  //   Md Saiyem Raiyan
endmodule

module Single_cycle_datapath_for_I_Type_and_R_Type_instruction (
  output [3:0] Output
);

  wire clock_1_out, main_control_1_alu_source, main_control_1_memory_read, main_control_1_memory_to_register,
       main_control_1_memory_write, main_control_1_register_destination, main_control_1_write_control;
  wire [1:0] rom_1_data_2;
  wire [2:0] adder_1_out, multiplexer_1_out, register_1_q;
  wire [3:0] bit_extender_1_out, multiplexer_2_out, multiplexer_3_out, n4_bit_register_1_read_data_1,
       n4_bit_register_1_read_data_2, ram_1_data;
  wire [10:0] rom_1_data;

  Register #(.width(3)) register_1 (.D(adder_1_out), .Q(register_1_q), .clk(clock_1_out));  // open: en, clr
  Adder #(.width(3)) adder_1 (.a(register_1_q), .b(3'b001), .out(adder_1_out));  // open: cin, cout
  RAM #(.addrWidth(4), .dataWidth(4), .bus("separate")) ram_1 (
    .addr(Output), .din(n4_bit_register_1_read_data_2), .data(ram_1_data), .str(main_control_1_memory_write),
    .clk(clock_1_out), .ld(main_control_1_memory_read));  // open: sel, clr
  ROM #(.addrWidth(3), .dataWidth(13)) rom_1 (.addr(register_1_q), .data({rom_1_data_2, rom_1_data}));  // open: sel
  Main_Control main_control_1 (
    .Opcode(rom_1_data_2), .ALU_Source(main_control_1_alu_source),
    .Register_Destination(main_control_1_register_destination),
    .Memory_to_Register(main_control_1_memory_to_register), .Write_Control(main_control_1_write_control),
    .Memory_Read(main_control_1_memory_read), .Memory_Write(main_control_1_memory_write));
  Clock clock_1 (.out(clock_1_out));
  assign bit_extender_1_out = {{1{1'b0}}, rom_1_data[2:0]};  // Bit_Extender bit_extender_1
  Multiplexer #(.width(3)) multiplexer_1 (
    .in0(rom_1_data[5:3]), .in1(rom_1_data[2:0]), .out(multiplexer_1_out),
    .sel(main_control_1_register_destination));  // open: en
  Multiplexer #(.width(4)) multiplexer_2 (
    .in0(Output), .in1(ram_1_data), .out(multiplexer_2_out), .sel(main_control_1_memory_to_register));  // open: en
  _4_bit_register u_4_bit_register_1 (
    .Write_Register(multiplexer_1_out), .Clock(clock_1_out), .Read_Data_1(n4_bit_register_1_read_data_1),
    .in_1(rom_1_data[8:6]), .Read_Data_2(n4_bit_register_1_read_data_2), .in_4(rom_1_data[5:3]),
    .Write(main_control_1_write_control), .Write_Data(multiplexer_2_out));
  Multiplexer #(.width(4)) multiplexer_3 (
    .in0(n4_bit_register_1_read_data_2), .in1(bit_extender_1_out), .out(multiplexer_3_out),
    .sel(main_control_1_alu_source));  // open: en
  _4_Bit_ALU u_4_bit_alu_1 (
    .Input_1(n4_bit_register_1_read_data_1), .Input_2(multiplexer_3_out),
    .Operation_Select_Bits(rom_1_data[10:9]), .Output(Output));

  // Notes on the sheet:
  //   Program Counter
  //   contents of rom_1 (hex, n*v repeats v):
  //   cc1 20b
  //   Single cycle datapath for R-type and I-type instructions with main control
  //   Md Saiyem Raiyan
endmodule

module Main_Control (
  input  [1:0] Opcode,
  output ALU_Source,
  output Register_Destination,
  output Memory_to_Register,
  output Write_Control,
  output Memory_Read,
  output Memory_Write
);

  Decoder #(.select(2)) decoder_1 (
    .out0(Register_Destination), .out1(Memory_Read), .out2(Memory_Write), .sel(Opcode));  // open: out3, en
  or or_1 (ALU_Source, Memory_Read, Memory_Write);
  or or_2 (Write_Control, Register_Destination, Memory_Read);

  assign Memory_to_Register = Memory_Read;
endmodule
